// Logisim project 8-bit-adder.circ as structural Verilog: 2 circuits, main circuit SingleAdder
module SingleAdder (
  input  Ci,
  input  A,
  input  B,
  output Sum,
  output Co
);

  wire and_1_out, and_2_out, xor_1_out;

  xor xor_1 (xor_1_out, A, B);
  and and_1 (and_1_out, A, B);
  xor xor_2 (Sum, xor_1_out, Ci);
  and and_2 (and_2_out, xor_1_out, Ci);
  or or_1 (Co, and_2_out, and_1_out);
endmodule

module ByteAdder (
  input  B8,
  input  B7,
  input  B6,
  input  B5,
  input  B4,
  input  B3,
  input  B2,
  input  B1,
  input  A8,
  input  A7,
  input  A6,
  input  A5,
  input  A4,
  input  A3,
  input  A2,
  input  A1,
  input  Carry_In,
  output Co,
  output O8,
  output O7,
  output O6,
  output O5,
  output O4,
  output O3,
  output O2,
  output O1
);

  wire singleadder_1_co, singleadder_3_co, singleadder_4_co, singleadder_5_co, singleadder_6_co,
       singleadder_7_co, singleadder_8_co;

  SingleAdder singleadder_1 (.Ci(singleadder_4_co), .A(A7), .B(B7), .Sum(O7), .Co(singleadder_1_co));
  SingleAdder singleadder_2 (.Ci(singleadder_1_co), .A(A8), .B(B8), .Sum(O8), .Co(Co));
  SingleAdder singleadder_3 (.Ci(singleadder_6_co), .A(A5), .B(B5), .Sum(O5), .Co(singleadder_3_co));
  SingleAdder singleadder_4 (.Ci(singleadder_3_co), .A(A6), .B(B6), .Sum(O6), .Co(singleadder_4_co));
  SingleAdder singleadder_5 (.Ci(singleadder_8_co), .A(A3), .B(B3), .Sum(O3), .Co(singleadder_5_co));
  SingleAdder singleadder_6 (.Ci(singleadder_5_co), .A(A4), .B(B4), .Sum(O4), .Co(singleadder_6_co));
  SingleAdder singleadder_7 (.Ci(Carry_In), .A(A1), .B(B1), .Sum(O1), .Co(singleadder_7_co));
  SingleAdder singleadder_8 (.Ci(singleadder_7_co), .A(A2), .B(B2), .Sum(O2), .Co(singleadder_8_co));
endmodule
