// Logisim project ALU.circ as structural Verilog: 3 circuits, main circuit Logic
module ALU (
  input  [7:0] A,
  input  [7:0] B,
  input  [3:0] OpCode,
  output C,
  output O,
  output [7:0] R
);

  wire [7:0] arithmetic_1_r, logic_1_r, multiplexer_1_out, multiplexer_2_out, not_1_out, not_2_out;

  assign not_1_out = ~A;  // NOT_Gate not_1, 8 bits wide
  assign not_2_out = ~B;  // NOT_Gate not_2, 8 bits wide
  Multiplexer #(.width(8)) multiplexer_1 (.in0(A), .in1(not_1_out), .out(multiplexer_1_out), .sel(OpCode[0]));
  Multiplexer #(.width(8)) multiplexer_2 (.in0(B), .in1(not_2_out), .out(multiplexer_2_out), .sel(OpCode[1]));
  Arithmetic arithmetic_1 (
    .A(multiplexer_1_out), .B(multiplexer_2_out), .Sub(OpCode[2]), .R(arithmetic_1_r), .Carry(C), .Overflow(O));
  Logic logic_1 (.A(multiplexer_1_out), .B(B), .OpCode(OpCode[2:1]), .R(logic_1_r));
  Multiplexer #(.width(8)) multiplexer_3 (.in0(arithmetic_1_r), .in1(logic_1_r), .out(R), .sel(OpCode[3]));

  // Notes on the sheet:
  //   Flags
endmodule

module Logic (
  input  [7:0] A,
  input  [7:0] B,
  input  [1:0] OpCode,
  output [7:0] R
);

  wire [7:0] and_logic_1_out_3, or_logic_1_out_3, xor_logic_1_out_3;

  OR_Logic or_logic_1 (.in_1(A), .in_2(B), .out_3(or_logic_1_out_3));
  AND_Logic and_logic_1 (.in_1(A), .in_2(B), .out_3(and_logic_1_out_3));
  XOR_Logic xor_logic_1 (.in_1(A), .in_2(B), .out_3(xor_logic_1_out_3));
  Multiplexer #(.select(2), .width(8)) multiplexer_1 (
    .in0(or_logic_1_out_3), .in1(and_logic_1_out_3), .in2(xor_logic_1_out_3), .in3(A), .out(R), .sel(OpCode));
endmodule

module Arithmetic (
  input  [7:0] A,
  input  [7:0] B,
  input  Sub,
  output [7:0] R,
  output Carry,
  output Overflow
);

  wire oba_1_cout, oba_2_cout, oba_3_cout, oba_4_cout, oba_5_cout, oba_6_cout, oba_7_cout;

  OBA oba_1 (.A(A[0]), .B(B[0]), .Cin(Sub), .R(R[0]), .Cout(oba_1_cout));
  OBA oba_2 (.A(A[1]), .B(B[1]), .Cin(oba_1_cout), .R(R[1]), .Cout(oba_2_cout));
  OBA oba_3 (.A(A[2]), .B(B[2]), .Cin(oba_2_cout), .R(R[2]), .Cout(oba_3_cout));
  OBA oba_4 (.A(A[3]), .B(B[3]), .Cin(oba_3_cout), .R(R[3]), .Cout(oba_4_cout));
  OBA oba_5 (.A(A[4]), .B(B[4]), .Cin(oba_4_cout), .R(R[4]), .Cout(oba_5_cout));
  OBA oba_6 (.A(A[5]), .B(B[5]), .Cin(oba_5_cout), .R(R[5]), .Cout(oba_6_cout));
  OBA oba_7 (.A(A[6]), .B(B[6]), .Cin(oba_6_cout), .R(R[6]), .Cout(oba_7_cout));
  OBA oba_8 (.A(A[7]), .B(B[7]), .Cin(oba_7_cout), .R(R[7]), .Cout(Carry));
  xor xor_1 (Overflow, Carry, oba_7_cout);

  // Notes on the sheet:
  //   Subtracts if either A or B is inverted first!!
endmodule
