// Logisim project OneBitAdder.circ as structural Verilog: 1 circuit, main circuit OBA
module OBA (
  input  A,
  input  B,
  input  Cin,
  output R,
  output Cout
);

  wire and_1_out, and_2_out, xor_1_out;

  xor xor_1 (xor_1_out, A, B);
  and and_1 (and_1_out, A, B);
  xor xor_2 (R, xor_1_out, Cin);
  and and_2 (and_2_out, xor_1_out, Cin);
  or or_1 (Cout, and_2_out, and_1_out);
endmodule
